# Fritzing sketch nadajnik_schemat (saved by Fritzing 0.9.3b)
breadboards: 1

parts:
  LED1 = smd LED [color="Red (633nm)" package="0805 [SMD]"]
  R1 = Resistor [tolerance=±5% resistance=330 package="1206 [SMD]"]
  U1 = atmega328 [package=dip]
  XTAL1 = Crystal [frequency="16 Mhz" package=THT]
  R2 = Resistor [tolerance=±5% resistance=220 package="1206 [SMD]"]
  VCC1 = Battery
  Transmiter_433Mhz = mystery part, 3 pins [chip_label=?]
  S1 = Reed switch [package=THT]
  S2 = Reed switch [package=THT]

nets:
  N1: LED1.cathode, U1.GND#7, R2.Pin_0, Transmiter_433Mhz.pin1, S1.pin_1
  N2: LED1.anode, R1.Pin_1
  N3: R1.Pin_0, U1.D10_(PWM)
  N4: U1.RESET, R2.Pin_1
  N5: U1.VCC, VCC1.+, Transmiter_433Mhz.pin3
  N6: U1.XLAT2, XTAL1.pin_0
  N7: U1.D5_(PWM), XTAL1.pin_1
  N8: U1.D9_(PWM), S2.pin_1
  N9: U1.D12, Transmiter_433Mhz.pin2
  N10: VCC1.-, S1.pin_2, S2.pin_2
